// Logisim project inciso a.circ as structural Verilog: 1 circuit, main circuit main
module main (
  input  x,
  input  y,
  input  z,
  output F
);

  wire and_1_out, and_2_out, not_1_out;

  not not_1 (not_1_out, y);
  and and_1 (and_1_out, x, y, z);
  and and_2 (and_2_out, x, not_1_out, z);
  xor xor_1 (F, and_1_out, and_2_out);
endmodule
