// Logisim project inciso c.circ as structural Verilog: 1 circuit, main circuit main
module main (
  input  x,
  input  y,
  input  z,
  output F
);

  wire not_1_out;

  not not_1 (not_1_out, z);
  and and_1 (F, x, not_1_out);
endmodule
